# Fritzing sketch ira (saved by Fritzing 0.9.3b)
circuit board: 8.46667cm x 5.64444cm
breadboards: 1

parts:
  Part1 = Arduino Mega 2560 (Rev3)
  Part2 = Arduino Nano (Rev3.0)
  NME0505SC = IC, DIP package, 4 pins [chip_label=NME0505SC]
  6N137 = IC, DIP package, 8 pins [chip_label=6N137]
  R1 = Resistor [tolerance=±5% resistance=4.7k package=THT]
  R3 = Resistor [tolerance=±5% resistance=330 package=THT]
  Raspberry_Pi_1 = Raspberry Pi 3 [part_number=RPI-3-V1.2]
  C3 = Ceramic Capacitor [capacitance=100nF package="100 mil [THT, multilayer]"]
  Power_Supply = mystery part, 7 pins [chip_label="Power Supply"]
  U1 = MAX485 [package=dil08]
  R2 = Resistor [tolerance=±5% resistance=470 package=THT]
  C4 = Ceramic Capacitor [capacitance=100nF package="100 mil [THT, multilayer]"]
  C5 = Ceramic Capacitor [capacitance=100nF package="100 mil [THT, multilayer]"]
  R4 = Resistor [tolerance=±5% resistance=120 package=THT]
  U2 = mystery part, 3 pins [chip_label=xlr]
  Lights = mystery part, 8 pins [chip_label=ws2813]
  Power_Supply3 = mystery part, 7 pins [chip_label="Power Supply"]
  Lights4 = mystery part, 8 pins [chip_label=ws2813]
  Power_Supply4 = mystery part, 7 pins [chip_label="Power Supply"]
  Power_Supply5 = mystery part, 7 pins [chip_label="Power Supply"]
  Lights5 = mystery part, 8 pins [chip_label=ws2813]
  Lights6 = mystery part, 8 pins [chip_label=ws2813]
  AC = AC Power [voltage=120V frequency=60]

nets:
  N1: Part1.D21/SCL, Part2.A4
  N2: Part1.D20/SDA, Part2.A5
  N3: Part1.D6_PWM, R3.Pin_0
  N4: Part2.D0/RX, 6N137.pin6, R1.Pin_1
  GND: Part2.GND, NME0505SC.pin1, NME0505SC.pin3, 6N137.pin5, C3.0, U1.RE, U1.DE, U1.GND, C4.0, C5.0, U2.pin1
  N5: Part2.D13/SCK, Raspberry_Pi_1.GPIO21
  N6: NME0505SC.pin2, 6N137.pin7
  N7: NME0505SC.pin4, 6N137.pin2, C3.1, U1.VCC, C4.1, C5.1
  N8: 6N137.pin3, R2.Pin_0
  N9: 6N137.pin8, R1.Pin_0
  N10: R3.Pin_1, Lights.pin2, Lights.pin3, Lights4.pin2, Lights4.pin3, Lights5.pin2, Lights5.pin3, Lights6.pin2, Lights6.pin3
  N11: Power_Supply.pin1, Power_Supply3.pin1, Power_Supply4.pin1, Power_Supply5.pin1, AC.V+
  N12: Power_Supply.pin2, Power_Supply3.pin2, Power_Supply4.pin2, Power_Supply5.pin2, AC.V-
  GND_2: Power_Supply.pin3, Power_Supply3.pin3, Power_Supply4.pin3, Power_Supply5.pin3
  N13: Power_Supply.pin4, Lights.pin4
  N14: Power_Supply.pin5, Lights.pin5
  N15: Power_Supply.pin6, Lights.pin1
  N16: Power_Supply.pin7, Lights.pin8
  N17: U1.RO, R2.Pin_1
  N18: U1.A, R4.Pin_0, U2.pin2
  N19: U1.B, R4.Pin_1, U2.pin3
  N20: Power_Supply3.pin4, Lights4.pin4
  N21: Power_Supply3.pin5, Lights4.pin5
  N22: Power_Supply3.pin6, Lights4.pin1
  N23: Power_Supply3.pin7, Lights4.pin8
  N24: Power_Supply4.pin4, Lights5.pin4
  N25: Power_Supply4.pin5, Lights5.pin5
  N26: Power_Supply4.pin6, Lights5.pin1
  N27: Power_Supply4.pin7, Lights5.pin8
  N28: Power_Supply5.pin4, Lights6.pin4
  N29: Power_Supply5.pin5, Lights6.pin5
  N30: Power_Supply5.pin6, Lights6.pin1
  N31: Power_Supply5.pin7, Lights6.pin8
